# Fritzing sketch freezerbuddy (saved by Fritzing 0.9.10b)
circuit board: 6.1888cm x 5.09679cm
breadboards: 1

parts:
  RELAY = RELAY-SOLIDSTATE [package=relay-s108t02]
  ARD_NANO = Arduino Nano (Rev3.0)
  HLK-PM1 = HLK-PM12 [part_number=HLK-PM12]
  DISP = male pin header, 4 pins [form="♂ (male)"]
  TEMP = male pin header, 3 pins [form="♂ (male)"]
  AC_IN = Camdenboss CTB0158-4 [part_number=CTB0158-4 package=THT]

nets:
  N1: RELAY.T1, AC_IN.pin4
  N2: RELAY.T2, HLK-PM1.AC_2, AC_IN.pin1
  N3: RELAY.+, ARD_NANO.D2
  N4: RELAY.-, ARD_NANO.GND, HLK-PM1.-Vo, DISP.pin4, TEMP.pin3
  N5: ARD_NANO.D4, DISP.pin1
  N6: ARD_NANO.D5, DISP.pin2
  N7: ARD_NANO.D10, TEMP.pin1
  N8: ARD_NANO.VIN, HLK-PM1.+Vo, DISP.pin3, TEMP.pin2
  N9: HLK-PM1.AC_1, AC_IN.pin2, AC_IN.pin3

notes:
  AC IN
  AC OUT
  +
  -
  D
  freezerbuddy v1
  CLK
  DIO
